# Fritzing sketch Fairy Lights (saved by Fritzing 0.9.8b)
breadboards: 1

parts:
  Mod1 = Raspberry Pi Pico
  U1 = TRANSISTOR_NPN_2 [package=to-92]
  R1 = Resistor [tolerance=±5% power=0.25 resistance=1k package=THT]
  J1 = screw terminal, 4 pins
  R2 = Resistor [tolerance=±5% power=0.25 resistance=10 package=THT]

nets:
  N1: Mod1.pin_3, Mod1.pin_8, Mod1.pin_13, Mod1.pin_18, Mod1.pin_23, Mod1.pin_28, Mod1.pin_33, Mod1.pin_38, U1.E
  N2: Mod1.pin_20, R1.Pin_1
  N3: Mod1.pin_36, R2.Pin_1
  N4: U1.C, J1.pin2
  N5: U1.B, R1.Pin_0
  N6: J1.pin4, R2.Pin_0

custom parts:
  Raspberry Pi Pico: Raspberry Pi Pico. Based around the RP2040 microcontroller the Pico is a low cost microcontroller device bringing Raspberry Pi quality, cost, and easy of use to the microcontroller space. Jan 2021, Split part in to two versions: tht (this one) and SMD. This one will drill holes for a .1 in header in pcb to allow plugging in the module as well as providing pads to solder the module to the top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
